# Fritzing sketch prototype_circuit (saved by Fritzing 0.9.3b)
breadboards: 1

parts:
  Part1 = Adafruit USB Type C Breakout [part_number=4090]
  S1 = Toggle Switch [package=THT]
  R1 = Resistor [tolerance=±5% resistance=5.1k package="2010 [SMD]"]
  R2 = Resistor [tolerance=±5% resistance=5.1k package="2010 [SMD]"]

nets:
  N1: Part1.GND, S1.L1, R1.Pin_1, R2.Pin_1
  N2: Part1.CC1, R1.Pin_0
  N3: Part1.CC2, R2.Pin_0

notes:
  VBUS, D-, D+, ID, GND,

custom parts:
  Adafruit USB Type C Breakout: Adafruit breakout board for USB Type C socket.
